// Logisim project 1sand2s.circ as structural Verilog: 1 circuit, main circuit main
module main (
  input  [1:0] in_1,
  input  [1:0] in_2,
  input  in_3,
  output [1:0] out_4,
  output [2:0] out_5
);

  wire and_1_out, not_3_out, not_4_out;

  not not_1 (out_4[0], in_1[0]);
  not not_2 (out_4[1], in_1[1]);
  not not_3 (not_3_out, in_2[0]);
  not not_4 (not_4_out, in_2[1]);
  xor xor_1 (out_5[0], not_3_out, in_3);
  and and_1 (and_1_out, in_3, not_3_out);
  xor xor_2 (out_5[1], and_1_out, not_4_out);
  and and_2 (out_5[2], not_4_out, and_1_out);

  // Notes on the sheet:
  //   2s complement
  //   1s complement
endmodule
