// Logisim project 2_bit_mag_comparator.circ as structural Verilog: 1 circuit, main circuit main
module main (
  input  B0,
  input  A1,
  input  A0,
  input  B1,
  input  in_5,
  output e,
  output g,
  output l
);

  wire and_1_out, and_2_out, and_3_out, and_4_out, and_5_out, and_7_out, and_8_out, and_9_out, and_10_out,
       and_11_out, and_12_out, and_13_out, not_1_out, not_2_out, not_3_out, not_4_out, xnor_1_out, xnor_2_out;
  wire [1:0] O0_out;

  not not_1 (not_1_out, A1);
  not not_2 (not_2_out, A0);
  not not_3 (not_3_out, B1);
  not not_4 (not_4_out, B0);
  xnor xnor_1 (xnor_1_out, A1, B1);
  xnor xnor_2 (xnor_2_out, A0, B0);
  and and_1 (and_1_out, A0, not_4_out);
  and and_2 (and_2_out, A1, not_3_out);
  and and_3 (and_3_out, not_1_out, B1);
  and and_4 (and_4_out, B0, not_2_out);
  and and_5 (and_5_out, xnor_1_out, and_1_out);
  and and_6 (e, xnor_1_out, xnor_2_out);
  and and_7 (and_7_out, xnor_1_out, and_4_out);
  or or_1 (g, and_5_out, and_2_out);
  or or_2 (l, and_3_out, and_7_out);
  and and_8 (and_8_out, A1, e);
  and and_9 (and_9_out, e, B0);
  and and_10 (and_10_out, g, A0);
  and and_11 (and_11_out, g, A1);
  and and_12 (and_12_out, B1, l);
  and and_13 (and_13_out, l, B0);
  or O1 (O0_out[1], and_11_out, and_8_out, and_12_out);
  or O0 (O0_out[0], and_10_out, and_9_out, and_13_out);
  Hex_Digit_Display #(.decimalPoint("false")) hex_digit_display_1 (.value({{2{in_5}}, O0_out}));

  // Notes on the sheet:
  //   DISPLAY THE GREATEST NUMBER
endmodule
