// Logisim project 4_bit_comp_nor.circ as structural Verilog: 3 circuits, main circuit main
module main (
  input  [3:0] in_1,
  input  [3:0] in_2
);

  wire fourinpand_1_op, nor_1_out, nor_2_out, nor_3_out, nor_4_out, nor_5_out, nor_6_out, nor_7_out,
       nor_8_out, xnorgate_1_axnorb, xnorgate_2_axnorb, xnorgate_4_axnorb;

  nor nor_1 (nor_1_out, in_1[3], in_1[3]);
  nor nor_2 (nor_2_out, in_1[2], in_1[2]);
  Hex_Digit_Display #(.decimalPoint("false")) hex_digit_display_1 (.value(in_1));
  nor nor_3 (nor_3_out, in_1[1], in_1[1]);
  nor nor_4 (nor_4_out, in_1[0], in_1[0]);
  nor nor_5 (nor_5_out, in_2[3], in_2[3]);
  nor nor_6 (nor_6_out, in_2[2], in_2[2]);
  nor nor_7 (nor_7_out, in_2[1], in_2[1]);
  Hex_Digit_Display #(.decimalPoint("false")) hex_digit_display_2 (.value(in_2));
  nor nor_8 (nor_8_out, in_2[0], in_2[0]);
  xnorgate xnorgate_1 (.A(in_2[3]), .B(in_1[3]), .Axnorb(xnorgate_1_axnorb));
  xnorgate xnorgate_2 (.A(in_1[0]), .B(in_2[0]), .Axnorb(xnorgate_2_axnorb));
  xnorgate xnorgate_3 (.A(in_1[1]), .B(in_2[1]), .Axnorb(xnorgate_1_axnorb));
  xnorgate xnorgate_4 (.A(in_2[2]), .B(in_1[2]), .Axnorb(xnorgate_4_axnorb));
  fourinpAND fourinpand_1 (
    .A(xnorgate_2_axnorb), .B(xnorgate_4_axnorb), .C(xnorgate_1_axnorb), .D(xnorgate_1_axnorb),
    .op(fourinpand_1_op));
  LED led_1 (.in(fourinpand_1_op));

  // Notes on the sheet:
  //   A3
  //   A2
  //   A1
  //   A
  //   A0
  //   B3
  //   B2
  //   B1
  //   B
  //   B0
  //   A=B
endmodule

module xnorgate (
  input  A,
  input  B,
  output Axnorb
);

  wire nor_1_out, nor_2_out, nor_3_out;

  nor nor_1 (nor_1_out, A, B);
  nor nor_2 (nor_2_out, A, nor_1_out);
  nor nor_3 (nor_3_out, nor_1_out, B);
  nor nor_4 (Axnorb, nor_2_out, nor_3_out);
endmodule

module fourinpAND (
  input  A,
  input  B,
  input  C,
  input  D,
  output op
);

  wire nor_1_out, nor_2_out, nor_3_out, nor_4_out, nor_5_out, nor_6_out, nor_7_out, nor_8_out;

  nor nor_1 (nor_1_out, A, A);
  nor nor_2 (nor_2_out, B, B);
  nor nor_3 (nor_3_out, nor_1_out, nor_2_out);
  nor nor_4 (nor_4_out, nor_3_out, nor_3_out);
  nor nor_5 (nor_5_out, C, C);
  nor nor_6 (nor_6_out, nor_4_out, nor_5_out);
  nor nor_7 (nor_7_out, nor_6_out, nor_6_out);
  nor nor_8 (nor_8_out, D, D);
  nor nor_9 (op, nor_7_out, nor_8_out);
endmodule
