// Logisim project 9base_adder.circ as structural Verilog: 1 circuit, main circuit main
module main (
  input  C,
  input  [3:0] in_2,
  input  [3:0] in_3,
  input  C_2,
  input  X,
  input  in_6
);

  wire and_1_out, and_2_out, and_3_out, and_4_out, and_5_out, and_6_out, and_7_out, and_8_out, and_9_out,
       and_10_out, and_11_out, and_12_out, and_13_out, and_14_out, and_15_out, and_16_out, and_17_out,
       and_18_out, not_1_out, or_1_out, or_2_out, or_3_out, or_4_out, or_6_out, or_7_out, or_8_out,
       xor_1_out, xor_2_out, xor_3_out, xor_4_out, xor_5_out, xor_6_out, xor_7_out, xor_8_out, xor_9_out,
       xor_11_out, xor_13_out;
  wire [0:0] or_5_out;
  wire [3:0] xor_10_out;

  Hex_Digit_Display hex_digit_display_1 (.value(in_2));  // open: dp
  Hex_Digit_Display hex_digit_display_2 (.value({{3{in_6}}, or_5_out[0]}));  // open: dp
  Hex_Digit_Display hex_digit_display_3 (.value(xor_10_out));  // open: dp
  Hex_Digit_Display hex_digit_display_4 (.value(in_3));  // open: dp
  xor xor_1 (xor_1_out, C, in_2[0]);
  and and_1 (and_1_out, C, in_2[0]);
  xor xor_2 (xor_2_out, xor_1_out, in_3[0]);
  and and_2 (and_2_out, xor_1_out, in_3[0]);
  or or_1 (or_1_out, and_2_out, and_1_out);
  xor xor_3 (xor_3_out, or_1_out, in_2[1]);
  and and_3 (and_3_out, or_1_out, in_2[1]);
  xor xor_4 (xor_4_out, xor_3_out, in_3[1]);
  and and_4 (and_4_out, xor_3_out, in_3[1]);
  or or_2 (or_2_out, and_4_out, and_3_out);
  xor xor_5 (xor_5_out, or_2_out, in_3[2]);
  and and_5 (and_5_out, or_2_out, in_3[2]);
  xor xor_6 (xor_6_out, xor_5_out, in_2[2]);
  and and_6 (and_6_out, xor_5_out, in_2[2]);
  or or_3 (or_3_out, and_6_out, and_5_out);
  xor xor_7 (xor_7_out, or_3_out, in_2[3]);
  and and_7 (and_7_out, or_3_out, in_2[3]);
  xor xor_8 (xor_8_out, xor_7_out, in_3[3]);
  and and_8 (and_8_out, xor_7_out, in_3[3]);
  not not_1 (not_1_out, xor_8_out);
  or or_4 (or_4_out, and_8_out, and_7_out);
  and and_9 (and_9_out, xor_6_out, xor_8_out);
  and and_10 (and_10_out, xor_8_out, xor_4_out);
  and and_11 (and_11_out, xor_8_out, xor_2_out);
  and and_12 (and_12_out, not_1_out, or_4_out);
  or or_5 (or_5_out[0], and_9_out, and_10_out, and_11_out, and_12_out);
  xor xor_9 (xor_9_out, C_2, xor_2_out);
  and and_13 (and_13_out, C_2, xor_2_out);
  xor xor_10 (xor_10_out[0], xor_9_out, or_5_out[0]);
  and and_14 (and_14_out, xor_9_out, or_5_out[0]);
  or or_6 (or_6_out, and_14_out, and_13_out);
  and and_15 (and_15_out, or_6_out, xor_4_out);
  xor xor_11 (xor_11_out, or_6_out, xor_4_out);
  xor xor_12 (xor_10_out[1], xor_11_out, or_5_out[0]);
  and and_16 (and_16_out, xor_11_out, or_5_out[0]);
  or or_7 (or_7_out, and_16_out, and_15_out);
  xor xor_13 (xor_13_out, or_7_out, or_5_out[0]);
  and and_17 (and_17_out, or_7_out, or_5_out[0]);
  xor xor_14 (xor_10_out[2], xor_13_out, xor_6_out);
  and and_18 (and_18_out, xor_13_out, xor_6_out);
  or or_8 (or_8_out, and_18_out, and_17_out);
  ExactlyOne xor_15 (.out(xor_10_out[3]), .in0(or_8_out), .in1(xor_8_out), .in2(X));

  // Notes on the sheet:
  //   +
  //   C
  //   S3
  //   S1
  //   S2
  //   S0
  //   X
  //   X
  //   LSB
  //   MSB
endmodule
