// Logisim project add_when_equal_else_subtract.circ as structural Verilog: 1 circuit, main circuit main
module main (
  input  in_1,
  input  in_2,
  output E,
  output SUM,
  output CARRY,
  output DIFF,
  output BOR
);

  wire EandA_out, EandB_out, not_1_out, not_2_out, NotEandA_out, NotEandB_out;

  xnor xnor_1 (E, in_1, in_2);
  and EandB (EandB_out, in_2, E);
  and EandA (EandA_out, in_1, E);
  not not_1 (not_1_out, E);
  and NotEandA (NotEandA_out, in_1, not_1_out);
  and NotEandB (NotEandB_out, not_1_out, in_2);
  not not_2 (not_2_out, NotEandA_out);
  xor xor_1 (SUM, EandB_out, EandA_out);
  and and_1 (CARRY, EandB_out, EandA_out);
  xor xor_2 (DIFF, NotEandA_out, NotEandB_out);
  and and_2 (BOR, not_2_out, NotEandB_out);
endmodule
