// Logisim project full_subt.circ as structural Verilog
module halfsub (
  input  A,
  input  B,
  input  in_3,
  input  in_4,
  input  in_5,
  output D,
  output BORROW,
  output out_8,
  output out_9
);

  wire and_2_out, and_3_out, and_4_out, not_1_out, not_2_out, xor_2_out;

  not not_1 (not_1_out, A);
  not not_2 (not_2_out, in_3);
  xor xor_1 (D, A, B);
  and and_1 (BORROW, not_1_out, B);
  xor xor_2 (xor_2_out, in_3, in_4);
  and and_2 (and_2_out, not_2_out, in_4);
  and and_3 (and_3_out, not_2_out, in_5);
  and and_4 (and_4_out, in_5, in_4);
  xor xor_3 (out_8, xor_2_out, in_5);
  or or_1 (out_9, and_3_out, and_2_out, and_4_out);

  // Notes on the sheet:
  //   a-b
  //   a-b-c
endmodule
