// Logisim project lab_bcd_adder_via_module.circ as structural Verilog: 2 circuits, main circuit main
module main (
  input  C,
  input  [3:0] in_2,
  input  [3:0] B,
  input  in_4,
  input  in_5
);

  wire and_1_out, and_2_out, fourbitadder_1_cf, fourbitadder_1_s0, fourbitadder_1_s1, fourbitadder_1_s2,
       fourbitadder_1_s3, fourbitadder_2_cf;
  wire [0:0] or_1_out;
  wire [3:0] fourbitadder_2_s0;

  Hex_Digit_Display hex_digit_display_1 (.value(in_2));  // open: dp
  Hex_Digit_Display hex_digit_display_2 (.value({{3{in_5}}, or_1_out[0]}));  // open: dp
  Hex_Digit_Display hex_digit_display_3 (.value(fourbitadder_2_s0));  // open: dp
  Hex_Digit_Display hex_digit_display_4 (.value(B));  // open: dp
  fourbitadder fourbitadder_1 (
    .C(C), .A0(in_2[0]), .A1(in_2[1]), .in_4(in_2[2]), .A3(in_2[3]), .B0(B[0]), .B1(B[1]), .B2(B[2]),
    .B3(B[3]), .S0(fourbitadder_1_s0), .S1(fourbitadder_1_s1), .S2(fourbitadder_1_s2),
    .S3(fourbitadder_1_s3), .Cf(fourbitadder_1_cf));
  and and_1 (and_1_out, fourbitadder_1_s1, fourbitadder_1_s3);
  and and_2 (and_2_out, fourbitadder_1_s2, fourbitadder_1_s3);
  or or_1 (or_1_out[0], and_1_out, and_2_out, fourbitadder_1_cf);
  fourbitadder fourbitadder_2 (
    .C(in_4), .A0(fourbitadder_1_s0), .A1(fourbitadder_1_s1), .in_4(fourbitadder_1_s2),
    .A3(fourbitadder_1_s3), .B0(in_4), .B1(or_1_out[0]), .B2(or_1_out[0]), .B3(in_4),
    .S0(fourbitadder_2_s0[0]), .S1(fourbitadder_2_s0[1]), .S2(fourbitadder_2_s0[2]),
    .S3(fourbitadder_2_s0[3]), .Cf(fourbitadder_2_cf));

  // Notes on the sheet:
  //   BCD_1
  //   +
  //   BCD_0
  //   A
endmodule

module fourbitadder (
  input  C,
  input  A0,
  input  A1,
  input  in_4,
  input  A3,
  input  B0,
  input  B1,
  input  B2,
  input  B3,
  output S0,
  output S1,
  output S2,
  output S3,
  output Cf
);

  wire and_1_out, and_2_out, and_3_out, and_4_out, and_5_out, and_6_out, and_7_out, and_8_out, or_1_out,
       or_2_out, or_3_out, X0_out, X1_out, X2_out, X3_out, xor_1_out, xor_3_out, xor_5_out, xor_7_out;

  xor X0 (X0_out, A0, C);
  xor X1 (X1_out, A1, C);
  xor X2 (X2_out, in_4, C);
  xor X3 (X3_out, A3, C);
  xor xor_1 (xor_1_out, C, X0_out);
  and and_1 (and_1_out, C, X0_out);
  xor xor_2 (S0, xor_1_out, B0);
  and and_2 (and_2_out, xor_1_out, B0);
  or or_1 (or_1_out, and_2_out, and_1_out);
  xor xor_3 (xor_3_out, or_1_out, X1_out);
  and and_3 (and_3_out, or_1_out, X1_out);
  xor xor_4 (S1, xor_3_out, B1);
  and and_4 (and_4_out, xor_3_out, B1);
  or or_2 (or_2_out, and_4_out, and_3_out);
  xor xor_5 (xor_5_out, or_2_out, X2_out);
  and and_5 (and_5_out, or_2_out, X2_out);
  xor xor_6 (S2, xor_5_out, B2);
  and and_6 (and_6_out, xor_5_out, B2);
  xor xor_7 (xor_7_out, or_3_out, X3_out);
  and and_7 (and_7_out, or_3_out, X3_out);
  or or_3 (or_3_out, and_6_out, and_5_out);
  and and_8 (and_8_out, xor_7_out, B3);
  xor xor_8 (S3, xor_7_out, B3);
  or or_4 (Cf, and_8_out, and_7_out);

  // Notes on the sheet:
  //   X
  //   Y
  //   C
  //   SUM/DIFF
endmodule
