// Logisim project lab_gray_bin_vice_versa.circ as structural Verilog: 1 circuit, main circuit main
module main (
  input  B3,
  input  B2,
  input  B1,
  input  g3,
  input  B0,
  input  g2,
  input  g1,
  input  g0,
  output G3_2,
  output G2_2,
  output G1_2,
  output G0_2,
  output b3_2,
  output b2_2,
  output b2_3,
  output out_16
);

  xor xor_1 (G2_2, B3, B2);
  xor xor_2 (G1_2, B2, B1);
  xor xor_3 (G0_2, B1, B0);
  xor xor_4 (b2_2, g3, g2);
  xor xor_5 (b2_3, b2_2, g1);
  xor xor_6 (out_16, b2_3, g0);

  assign b3_2 = g3;
  assign G3_2 = B3;
endmodule
