// Logisim project lab_mpxer.circ as structural Verilog: 1 circuit, main circuit main
module main (
  input  A,
  input  B,
  input  C,
  input  in_4,
  input  in_5,
  input  in_6,
  input  in_7,
  input  in_8,
  input  in_9,
  input  in_10,
  input  in_11,
  input  in_12,
  input  in_13,
  input  in_14,
  output D0,
  output D1,
  output D2,
  output D3,
  output D4,
  output out_20,
  output D5,
  output D6,
  output D7
);

  wire and_9_out, and_10_out, and_11_out, and_12_out, and_13_out, and_14_out, and_15_out, and_16_out,
       and_17_out, and_18_out, and_19_out, and_20_out, and_21_out, and_22_out, and_23_out, and_24_out,
       not_1_out, not_2_out, not_3_out, not_4_out, not_5_out, not_6_out;

  not not_1 (not_1_out, A);
  not not_2 (not_2_out, B);
  not not_3 (not_3_out, C);
  and and_1 (D0, not_1_out, not_2_out, not_3_out);
  and and_2 (D1, not_1_out, not_2_out, C);
  and and_3 (D2, not_1_out, B, not_3_out);
  and and_4 (D3, not_1_out, B, C);
  and and_5 (D4, A, not_2_out, not_3_out);
  and and_6 (D5, A, not_2_out, C);
  and and_7 (D6, A, B, not_3_out);
  and and_8 (D7, A, B, C);
  not not_4 (not_4_out, in_4);
  not not_5 (not_5_out, in_5);
  not not_6 (not_6_out, in_6);
  and and_9 (and_9_out, not_4_out, not_5_out, in_6);
  and and_10 (and_10_out, not_4_out, in_5, not_6_out);
  and and_11 (and_11_out, not_4_out, in_5, in_6);
  and and_12 (and_12_out, in_4, not_5_out, not_6_out);
  and and_13 (and_13_out, in_4, not_5_out, in_6);
  and and_14 (and_14_out, in_4, in_5, not_6_out);
  and and_15 (and_15_out, in_4, in_5, in_6);
  and and_16 (and_16_out, not_4_out, not_5_out, not_6_out);
  and and_17 (and_17_out, and_16_out, in_7);
  and and_18 (and_18_out, and_9_out, in_8);
  and and_19 (and_19_out, and_10_out, in_9);
  and and_20 (and_20_out, and_11_out, in_10);
  and and_21 (and_21_out, and_12_out, in_11);
  and and_22 (and_22_out, and_13_out, in_12);
  and and_23 (and_23_out, and_14_out, in_13);
  and and_24 (and_24_out, and_15_out, in_14);
  or or_1 (out_20, and_17_out, and_18_out, and_19_out, and_20_out, and_21_out, and_22_out, and_23_out, and_24_out);
endmodule
