// Logisim project only_nand.circ as structural Verilog
module or_gate (
  input  A,
  input  B,
  output AorB
);

  wire nand_1_out, nand_2_out;

  nand nand_1 (nand_1_out, A, A);
  nand nand_2 (nand_2_out, B, B);
  nand nand_3 (AorB, nand_1_out, nand_2_out);
endmodule

module and_gate (
  input  A,
  input  B,
  output AandB
);

  wire nand_1_out;

  nand nand_1 (nand_1_out, A, B);
  nand nand_2 (AandB, nand_1_out, nand_1_out);
endmodule

module not_gate (
  input  A,
  output notA
);

  nand nand_1 (notA, A, A);
endmodule

module xor_g (
  input  A,
  input  B,
  output Axorb
);

  wire nand_1_out, nand_2_out, nand_3_out;

  nand nand_1 (nand_1_out, A, B);
  nand nand_2 (nand_2_out, A, nand_1_out);
  nand nand_3 (nand_3_out, nand_1_out, B);
  nand nand_4 (Axorb, nand_2_out, nand_3_out);
endmodule

module xnor_g (
  input  A,
  input  B,
  output Axorb
);

  wire nand_1_out, nand_2_out, nand_3_out, nand_4_out;

  nand nand_1 (nand_1_out, A, B);
  nand nand_2 (nand_2_out, A, nand_1_out);
  nand nand_3 (nand_3_out, nand_1_out, B);
  nand nand_4 (nand_4_out, nand_2_out, nand_3_out);
  nand nand_5 (Axorb, nand_4_out, nand_4_out);
endmodule
