// Logisim project only_nor.circ as structural Verilog
module notgate (
  input  A,
  output Ac
);

  nor nor_1 (Ac, A, A);
endmodule

module andgate (
  input  A,
  input  B,
  output AandB
);

  wire nor_1_out, nor_2_out;

  nor nor_1 (nor_1_out, A, A);
  nor nor_2 (nor_2_out, B, B);
  nor nor_3 (AandB, nor_1_out, nor_2_out);
endmodule

module orgate (
  input  A,
  input  B,
  output AorB
);

  wire nor_1_out;

  nor nor_1 (nor_1_out, A, B);
  notgate notgate_1 (.A(nor_1_out), .Ac(AorB));
endmodule

module xorgate (
  input  in_1,
  input  in_2,
  output Axorb
);

  wire nor_1_out, nor_2_out, nor_3_out, nor_4_out;

  nor nor_1 (nor_1_out, in_1, in_2);
  nor nor_2 (nor_2_out, in_1, nor_1_out);
  nor nor_3 (nor_3_out, nor_1_out, in_2);
  nor nor_4 (nor_4_out, nor_2_out, nor_3_out);
  nor nor_5 (Axorb, nor_4_out, nor_4_out);
endmodule

module xnorgate (
  input  in_1,
  input  in_2,
  output Axnorb
);

  wire nor_1_out, nor_2_out, nor_3_out;

  nor nor_1 (nor_1_out, in_1, in_2);
  nor nor_2 (nor_2_out, in_1, nor_1_out);
  nor nor_3 (nor_3_out, nor_1_out, in_2);
  nor nor_4 (Axnorb, nor_2_out, nor_3_out);
endmodule
