// Logisim project BIN_TO_SEVENSEGMENT.circ as structural Verilog: 1 circuit, main circuit main
module main (
  input  [3:0] in_1
);

  wire a_out, and_1_out, and_2_out, and_3_out, and_4_out, and_5_out, and_6_out, and_7_out, b_out, c_out,
       d_out, e_out, f_out, g_out, not_1_out, not_2_out, not_3_out, not_4_out, xnor_1_out, xnor_2_out,
       xor_1_out;

  not not_1 (not_1_out, in_1[3]);
  not not_2 (not_2_out, in_1[2]);
  not not_3 (not_3_out, in_1[1]);
  not not_4 (not_4_out, in_1[0]);
  and and_1 (and_1_out, in_1[2], not_4_out);
  and and_2 (and_2_out, not_3_out, not_4_out);
  and and_3 (and_3_out, in_1[2], not_3_out);
  xnor xnor_1 (xnor_1_out, in_1[2], in_1[0]);
  xnor xnor_2 (xnor_2_out, in_1[1], in_1[0]);
  or c (c_out, in_1[2], in_1[0], not_3_out);
  and and_4 (and_4_out, not_2_out, not_4_out);
  and and_5 (and_5_out, not_2_out, in_1[1]);
  and and_6 (and_6_out, in_1[1], not_4_out);
  and and_7 (and_7_out, in_1[2], not_3_out, in_1[0]);
  xor xor_1 (xor_1_out, in_1[2], in_1[1]);
  or a (a_out, xnor_1_out, in_1[3], in_1[1]);
  or b (b_out, xnor_2_out, not_2_out);
  or d (d_out, and_4_out, and_5_out, and_6_out, and_7_out, in_1[3]);
  or e (e_out, and_4_out, and_6_out);
  or f (f_out, in_1[3], and_2_out, and_3_out, and_1_out);
  or g (g_out, in_1[3], and_1_out, xor_1_out);
  _7_Segment_Display #(.decimalPoint("false")) u_7_segment_display_1 (
    .g(g_out), .f(f_out), .a(a_out), .b(b_out), .e(e_out), .d(d_out), .c(c_out));

  // Notes on the sheet:
  //   X3 X2 X1 X0
  //   A
  //   B
  //   A'
  //   B'
  //   C
  //   D
  //   C'
  //   D'
  //   B XNOR D
  //   B XNOR C
endmodule
