// Logisim project ROLLNUMBERPRINT.circ as structural Verilog: 2 circuits, main circuit main
module main (
  input  SET,
  input  CLEAR
);

  wire and_1_out, and_2_out, clock_1_out, logic_1_a, logic_1_b, logic_1_c, logic_1_d, logic_1_e, logic_1_f,
       logic_1_g, not_1_out, or_1_out;
  wire [3:0] D_q;

  T_Flip_Flop A (.T(or_1_out), .clk(clock_1_out), .Q(D_q[3]), .reset(CLEAR), .preset(SET));  // open: Qn
  not not_1 (not_1_out, D_q[3]);
  T_Flip_Flop B (.T(and_2_out), .clk(clock_1_out), .Q(D_q[2]), .reset(CLEAR), .preset(SET));  // open: Qn
  Clock clock_1 (.out(clock_1_out));
  T_Flip_Flop C (.T(D_q[0]), .clk(clock_1_out), .Q(D_q[1]), .reset(CLEAR), .preset(SET));  // open: Qn
  and and_1 (and_1_out, D_q[2], D_q[1], D_q[0]);
  or or_1 (or_1_out, and_1_out, D_q[3]);
  and and_2 (and_2_out, D_q[1], D_q[0]);
  T_Flip_Flop D (.T(not_1_out), .clk(clock_1_out), .Q(D_q[0]), .reset(CLEAR), .preset(SET));  // open: Qn
  Hex_Digit_Display hex_digit_display_1 (.value(D_q));  // open: dp
  \logic  logic_1 (
    .a3(D_q[3]), .a2(D_q[2]), .a1(D_q[1]), .a0(D_q[0]), .a(logic_1_a), .b(logic_1_b), .c(logic_1_c),
    .d(logic_1_d), .e(logic_1_e), .f(logic_1_f), .g(logic_1_g));
  _7_Segment_Display #(.decimalPoint("false")) u_7_segment_display_1 (
    .g(logic_1_g), .f(logic_1_f), .a(logic_1_a), .b(logic_1_b), .e(logic_1_e), .d(logic_1_d), .c(logic_1_c));

  // Notes on the sheet:
  //   ASSUMPTION TRIGGER 1 to 9 is equivalent to 0 to 8 in 9 MOD COUNTER
  //   LOGIC TO GENERATE ROLL NUMBER IS IN SEPARATE MODULE CALLED "LOGIC"
  //   CS23B1011
endmodule

module \logic  (
  input  a3,
  input  a2,
  input  a1,
  input  a0,
  output a,
  output b,
  output c,
  output d,
  output e,
  output f,
  output g
);

  wire and_1_out, and_2_out, and_3_out, and_4_out, and_5_out, and_6_out, and_7_out, and_8_out, and_9_out,
       and_11_out, not_1_out, not_2_out, not_3_out, not_4_out;

  not not_1 (not_1_out, a3);
  not not_2 (not_2_out, a2);
  not not_3 (not_3_out, a1);
  not not_4 (not_4_out, a0);
  and and_1 (and_1_out, not_1_out, not_2_out);
  and and_2 (and_2_out, a1, not_4_out);
  and and_3 (and_3_out, a2, a0);
  or or_1 (c, a0, a2, a3);
  and and_4 (and_4_out, not_1_out, not_2_out);
  and and_5 (and_5_out, not_1_out, not_4_out);
  and and_6 (and_6_out, a2, not_4_out);
  and and_7 (and_7_out, not_1_out, not_2_out, not_3_out);
  and and_8 (and_8_out, not_2_out, a0);
  and and_9 (and_9_out, not_2_out, a1);
  or or_2 (a, and_1_out, and_2_out);
  or or_3 (b, a1, and_3_out, a3);
  or or_4 (d, and_4_out, and_5_out);
  and and_10 (e, not_1_out, not_4_out);
  or or_5 (f, and_6_out, and_7_out);
  or or_6 (g, and_8_out, and_9_out, and_11_out);
  and and_11 (and_11_out, a2, not_3_out, not_4_out);
endmodule
