// Logisim project ROLL_NUM_PRINT_MODULARIZED.circ as structural Verilog: 2 circuits, main circuit main
module main (
  input  [3:0] in_1,
  input  [3:0] in_2,
  input  [3:0] in_3,
  input  [3:0] in_4,
  input  [3:0] in_5,
  input  [3:0] in_6,
  input  [3:0] in_7,
  input  [3:0] in_8,
  input  [3:0] in_9,
  input  SET,
  input  CLEAR
);

  wire and_1_out, and_2_out, clock_1_out, not_1_out, or_1_out, sevenseg_1_a, sevenseg_1_b, sevenseg_1_c,
       sevenseg_1_d, sevenseg_1_e, sevenseg_1_f, sevenseg_1_g;
  wire [3:0] D_q, multiplexer_1_out;

  T_Flip_Flop A (.T(or_1_out), .clk(clock_1_out), .Q(D_q[3]), .reset(CLEAR), .preset(SET));  // open: Qn
  not not_1 (not_1_out, D_q[3]);
  T_Flip_Flop B (.T(and_2_out), .clk(clock_1_out), .Q(D_q[2]), .reset(CLEAR), .preset(SET));  // open: Qn
  Clock clock_1 (.out(clock_1_out));
  T_Flip_Flop C (.T(D_q[0]), .clk(clock_1_out), .Q(D_q[1]), .reset(CLEAR), .preset(SET));  // open: Qn
  and and_1 (and_1_out, D_q[2], D_q[1], D_q[0]);
  or or_1 (or_1_out, and_1_out, D_q[3]);
  and and_2 (and_2_out, D_q[1], D_q[0]);
  T_Flip_Flop D (.T(not_1_out), .clk(clock_1_out), .Q(D_q[0]), .reset(CLEAR), .preset(SET));  // open: Qn
  Multiplexer #(.select(4), .width(4)) multiplexer_1 (
    .in0(in_1), .in1(in_2), .in2(in_3), .in3(in_4), .in4(in_5), .in5(in_6), .in6(in_7), .in7(in_8),
    .in8(in_9), .out(multiplexer_1_out), .sel(D_q));  // open: in9, in10, in11, in12, in13, in14, in15
  Hex_Digit_Display hex_digit_display_1 (.value(D_q));  // open: dp
  SEVENSEG sevenseg_1 (
    .x3(multiplexer_1_out[3]), .x2(multiplexer_1_out[2]), .x1(multiplexer_1_out[1]),
    .x0(multiplexer_1_out[0]), .a(sevenseg_1_a), .b(sevenseg_1_b), .c(sevenseg_1_c), .d(sevenseg_1_d),
    .e(sevenseg_1_e), .f(sevenseg_1_f), .g(sevenseg_1_g));
  _7_Segment_Display #(.decimalPoint("false")) u_7_segment_display_1 (
    .g(sevenseg_1_g), .f(sevenseg_1_f), .a(sevenseg_1_a), .b(sevenseg_1_b), .e(sevenseg_1_e),
    .d(sevenseg_1_d), .c(sevenseg_1_c));

  // Notes on the sheet:
  //   in_1: initial=0x44c
  //   in_2: initial=0x5
  //   in_3: initial=0x2
  //   in_4: initial=0x3
  //   in_5: initial=0x44b
  //   in_6: initial=0x1
  //   in_8: initial=0x1
  //   in_9: initial=0x1
  //   C
  //   1100
  //   S
  //   0101
  //   2
  //   0010
  //   3
  //   0011
  //   b
  //   1011
  //   1
  //   0001
  //   0
  //   0000
  //   1
  //   0001
  //   1
  //   0001
  //   I HAVE MODULARIZED THE CIRCUIT; CREATED BINARY TO 7 SEGMENT DISPAY AND STORED IN CIRCUIT CALLED "SEVENSEG"
  //   CS23B1011
endmodule

module SEVENSEG (
  input  x3,
  input  x2,
  input  x1,
  input  x0,
  output a,
  output b,
  output c,
  output d,
  output e,
  output f,
  output g
);

  wire and_1_out, and_2_out, and_3_out, and_4_out, and_5_out, and_6_out, and_7_out, and_8_out, and_9_out,
       and_10_out, and_11_out, and_12_out, and_13_out, and_14_out, and_15_out, and_16_out, and_17_out,
       and_18_out, and_19_out, and_20_out, and_21_out, and_22_out, and_23_out, and_24_out, and_25_out,
       and_26_out, and_27_out, and_28_out, and_29_out, and_30_out, and_31_out, and_32_out, and_33_out,
       and_34_out, and_35_out, not_1_out, not_2_out, not_3_out, not_4_out;

  not not_1 (not_1_out, x3);
  not not_2 (not_2_out, x2);
  not not_3 (not_3_out, x1);
  not not_4 (not_4_out, x0);
  and and_1 (and_1_out, not_2_out, not_4_out);
  and and_2 (and_2_out, not_1_out, x1);
  and and_3 (and_3_out, not_1_out, x2, x0);
  and and_4 (and_4_out, x3, not_2_out, not_3_out);
  and and_5 (and_5_out, x3, not_4_out);
  and and_6 (and_6_out, x2, x1);
  and and_7 (and_7_out, not_1_out, not_3_out, not_4_out);
  and and_8 (and_8_out, not_1_out, x1, x0);
  and and_9 (and_9_out, not_2_out, not_4_out);
  and and_10 (and_10_out, x3, not_3_out, x0);
  and and_11 (and_11_out, not_1_out, not_2_out);
  and and_12 (and_12_out, not_1_out, x2);
  and and_13 (and_13_out, x3, not_2_out);
  and and_14 (and_14_out, not_3_out, x0);
  and and_15 (and_15_out, not_2_out, not_3_out);
  and and_16 (and_16_out, not_2_out, x0);
  and and_17 (and_17_out, x2, not_3_out, x0);
  and and_18 (and_18_out, not_1_out, not_2_out, not_4_out);
  and and_19 (and_19_out, not_2_out, x1, x0);
  and and_20 (and_20_out, x3, not_3_out);
  and and_21 (and_21_out, x2, x1, not_4_out);
  and and_22 (and_22_out, not_2_out, not_4_out);
  and and_23 (and_23_out, x1, not_4_out);
  and and_24 (and_24_out, x3, x1);
  and and_25 (and_25_out, x3, x2);
  and and_26 (and_26_out, not_3_out, not_4_out);
  and and_27 (and_27_out, not_1_out, x2, not_3_out);
  and and_28 (and_28_out, x2, not_4_out);
  and and_29 (and_29_out, x3, not_2_out);
  and and_30 (and_30_out, x3, x1);
  and and_31 (and_31_out, not_2_out, x1);
  and and_32 (and_32_out, x3, not_2_out);
  and and_33 (and_33_out, not_1_out, x2, not_3_out);
  and and_34 (and_34_out, x1, not_4_out);
  and and_35 (and_35_out, x3, x0);
  or or_1 (a, and_1_out, and_2_out, and_3_out, and_4_out, and_5_out, and_6_out);
  or or_2 (b, and_7_out, and_8_out, and_9_out, and_10_out, and_11_out);
  or or_3 (c, and_12_out, and_13_out, and_14_out, and_15_out, and_16_out);
  or or_4 (d, and_17_out, and_18_out, and_19_out, and_20_out, and_21_out);
  or or_5 (e, and_22_out, and_23_out, and_24_out, and_25_out);
  or or_6 (f, and_26_out, and_27_out, and_28_out, and_29_out, and_30_out);
  or or_7 (g, and_31_out, and_32_out, and_33_out, and_34_out, and_35_out);
  _7_Segment_Display #(.decimalPoint("false")) u_7_segment_display_1 (.g(g), .f(f), .a(a), .b(b), .e(e), .d(d), .c(c));
endmodule
