// Logisim project MOD_NINE_COUNTER.circ as structural Verilog: 1 circuit, main circuit main
module main (
  input  in_1,
  input  in_2
);

  wire and_1_out, and_2_out, and_3_out, clock_1_out, not_1_out, not_2_out;
  wire [3:0] t_ff_4_q;

  and and_1 (and_1_out, and_2_out, t_ff_4_q[2]);
  T_Flip_Flop t_ff_1 (.T(and_1_out), .clk(clock_1_out), .Q(t_ff_4_q[3]), .reset(and_3_out), .preset(in_1));  // open: Qn
  LED led_1 (.in(t_ff_4_q[3]));
  LED led_2 (.in(t_ff_4_q[2]));
  T_Flip_Flop t_ff_2 (.T(and_2_out), .clk(clock_1_out), .Q(t_ff_4_q[2]), .reset(and_3_out), .preset(in_1));  // open: Qn
  not not_1 (not_1_out, t_ff_4_q[2]);
  not not_2 (not_2_out, t_ff_4_q[1]);
  and and_2 (and_2_out, t_ff_4_q[0], t_ff_4_q[1]);
  T_Flip_Flop t_ff_3 (
    .T(t_ff_4_q[0]), .clk(clock_1_out), .Q(t_ff_4_q[1]), .reset(and_3_out), .preset(in_1));  // open: Qn
  and and_3 (and_3_out, t_ff_4_q[3], not_1_out, not_2_out, t_ff_4_q[0]);
  LED led_3 (.in(t_ff_4_q[1]));
  T_Flip_Flop t_ff_4 (.T(in_2), .clk(clock_1_out), .Q(t_ff_4_q[0]), .reset(and_3_out), .preset(in_1));  // open: Qn
  LED led_4 (.in(t_ff_4_q[0]));
  Hex_Digit_Display #(.decimalPoint("false")) hex_digit_display_1 (.value(t_ff_4_q));
  Clock clock_1 (.out(clock_1_out));

  // Notes on the sheet:
  //   in_2: initial=0x1
  //   UP-COUNTER
endmodule
