// Logisim project SEQ-1(ALL_BUILTIN_COUNTERS_REGISTERS).circ as structural Verilog: 4 circuits, main circuit main
module main (
  input  S,
  input  S_2,
  input  R,
  input  R_2,
  input  R_3,
  input  S_3,
  output out_7,
  output out_8,
  output out_9,
  output out_10,
  output out_11,
  output out_12
);

  wire nand_3_out, nand_4_out;

  nand nand_1 (out_7, out_9, S);
  nand nand_2 (out_9, out_7, R);
  nor nor_1 (out_11, out_12, R_3);
  nor nor_2 (out_12, out_11, S_3);
  nand nand_3 (nand_3_out, S_2, S_2);
  nand nand_4 (nand_4_out, R_2, R_2);
  nand nand_5 (out_8, out_10, nand_3_out);
  nand nand_6 (out_10, out_8, nand_4_out);

  // Notes on the sheet:
  //   SR LATCH(LOW_STATE)
  //   RS LATCH(HIGH STATE)
  //   SR LATCH(HIGH_STATE)
endmodule

module check_builtin (
  input  in_1,
  input  in_2,
  input  in_3,
  input  in_4,
  input  in_5,
  input  in_6,
  input  in_7,
  input  D,
  output out_9,
  output out_10,
  output out_11,
  output out_12
);

  wire clock_1_out, clock_2_out, clock_3_out, d_ff_1_q;

  Clock clock_1 (.out(clock_1_out));
  Clock clock_2 (.out(clock_2_out));
  S_R_Flip_Flop s_r_ff_1 (.S(in_3), .R(in_5), .clk(clock_1_out), .Q(out_9), .reset(in_1), .Qn(out_11), .preset(in_1));
  D_Flip_Flop d_ff_1 (.D(D), .clk(clock_2_out), .Q(d_ff_1_q), .preset(in_7), .reset(in_7));  // open: Qn
  LED led_1 (.in(d_ff_1_q));
  J_K_Flip_Flop j_k_ff_1 (.J(in_4), .K(in_6), .clk(clock_3_out), .Q(out_10), .Qn(out_12), .preset(in_2), .reset(in_2));
  Clock clock_3 (.out(clock_3_out));

  // Notes on the sheet:
  //   SR
  //   D
  //   JK
endmodule

module REG1STER (
  input  D,
  input  in_2,
  input  in_3,
  input  in_4,
  input  I0,
  input  I1,
  input  I2,
  input  I3,
  input  D_FOR_R_SHIFT,
  input  D_2,
  input  D_FOR_L_SHIFT,
  input  SELECT,
  input  SELECT_2,
  input  in_14,
  input  in_15,
  input  in_16,
  input  in_17,
  input  in_18,
  input  in_19,
  input  DATARIGHT,
  input  DATALEFT,
  input  [1:0] SELECTOR,
  input  SET,
  input  RESET
);

  wire clock_1_out, clock_2_out, clock_3_out, clock_4_out, clock_5_out, d_ff_1_q, d_ff_2_q, d_ff_3_q,
       d_ff_4_q, d_ff_5_q, d_ff_6_q, d_ff_7_q, d_ff_8_q, d_ff_9_q, d_ff_10_q, d_ff_11_q, d_ff_12_q,
       d_ff_13_q, d_ff_14_q, d_ff_15_q, d_ff_16_q, d_ff_17_q, d_ff_18_q, d_ff_19_q, d_ff_20_q,
       multiplexer_1_out, multiplexer_2_out, multiplexer_3_out, multiplexer_4_out, multiplexer_5_out,
       multiplexer_6_out, multiplexer_7_out, multiplexer_8_out, multiplexer_9_out, multiplexer_10_out,
       multiplexer_11_out, multiplexer_12_out;

  D_Flip_Flop d_ff_1 (.D(D), .clk(clock_1_out), .Q(d_ff_1_q), .preset(in_3), .reset(in_3));  // open: Qn
  Clock clock_1 (.out(clock_1_out));
  Clock clock_2 (.out(clock_2_out));
  Multiplexer multiplexer_1 (.in0(D_2), .in1(I0), .out(multiplexer_1_out), .sel(SELECT_2));
  D_Flip_Flop d_ff_2 (
    .D(multiplexer_1_out), .clk(clock_2_out), .Q(d_ff_2_q), .preset(in_15), .reset(in_15));  // open: Qn
  D_Flip_Flop d_ff_3 (.D(d_ff_1_q), .clk(clock_1_out), .Q(d_ff_3_q), .preset(in_3), .reset(in_3));  // open: Qn
  Multiplexer multiplexer_2 (.in0(d_ff_2_q), .in1(I1), .out(multiplexer_2_out), .sel(SELECT_2));
  D_Flip_Flop d_ff_4 (
    .D(multiplexer_2_out), .clk(clock_2_out), .Q(d_ff_4_q), .preset(in_15), .reset(in_15));  // open: Qn
  LED led_1 (.in(d_ff_1_q));
  LED led_2 (.in(d_ff_3_q));
  D_Flip_Flop d_ff_5 (.D(d_ff_3_q), .clk(clock_1_out), .Q(d_ff_5_q), .preset(in_3), .reset(in_3));  // open: Qn
  Multiplexer multiplexer_3 (.in0(d_ff_4_q), .in1(I2), .out(multiplexer_3_out), .sel(SELECT_2));
  D_Flip_Flop d_ff_6 (
    .D(multiplexer_3_out), .clk(clock_2_out), .Q(d_ff_6_q), .preset(in_15), .reset(in_15));  // open: Qn
  Clock clock_3 (.out(clock_3_out));
  LED led_3 (.in(d_ff_5_q));
  D_Flip_Flop d_ff_7 (.D(d_ff_5_q), .clk(clock_1_out), .Q(d_ff_7_q), .preset(in_3), .reset(in_3));  // open: Qn
  LED led_4 (.in(d_ff_2_q));
  LED led_5 (.in(d_ff_4_q));
  LED led_6 (.in(d_ff_8_q));
  Multiplexer #(.select(2)) multiplexer_4 (
    .in0(DATALEFT), .in1(d_ff_10_q), .in2(in_16), .in3(d_ff_8_q), .out(multiplexer_4_out), .sel(SELECTOR));
  D_Flip_Flop d_ff_8 (.D(multiplexer_4_out), .clk(clock_3_out), .Q(d_ff_8_q), .preset(SET), .reset(RESET));  // open: Qn
  LED led_7 (.in(d_ff_7_q));
  LED led_8 (.in(d_ff_6_q));
  LED led_9 (.in(d_ff_9_q));
  Multiplexer multiplexer_5 (.in0(d_ff_6_q), .in1(I3), .out(multiplexer_5_out), .sel(SELECT_2));
  D_Flip_Flop d_ff_9 (
    .D(multiplexer_5_out), .clk(clock_2_out), .Q(d_ff_9_q), .preset(in_15), .reset(in_15));  // open: Qn
  LED led_10 (.in(d_ff_10_q));
  LED led_11 (.in(d_ff_11_q));
  Multiplexer #(.select(2)) multiplexer_6 (
    .in0(d_ff_8_q), .in1(d_ff_11_q), .in2(in_17), .in3(d_ff_10_q), .out(multiplexer_6_out), .sel(SELECTOR));
  D_Flip_Flop d_ff_10 (
    .D(multiplexer_6_out), .clk(clock_3_out), .Q(d_ff_10_q), .preset(SET), .reset(RESET));  // open: Qn
  LED led_12 (.in(d_ff_12_q));
  Multiplexer #(.select(2)) multiplexer_7 (
    .in0(d_ff_10_q), .in1(d_ff_12_q), .in2(in_18), .in3(d_ff_11_q), .out(multiplexer_7_out), .sel(SELECTOR));
  D_Flip_Flop d_ff_11 (
    .D(multiplexer_7_out), .clk(clock_3_out), .Q(d_ff_11_q), .preset(SET), .reset(RESET));  // open: Qn
  Clock clock_4 (.out(clock_4_out));
  Multiplexer #(.select(2)) multiplexer_8 (
    .in0(d_ff_11_q), .in1(DATARIGHT), .in2(in_19), .in3(d_ff_12_q), .out(multiplexer_8_out), .sel(SELECTOR));
  D_Flip_Flop d_ff_12 (
    .D(multiplexer_8_out), .clk(clock_3_out), .Q(d_ff_12_q), .preset(SET), .reset(RESET));  // open: Qn
  D_Flip_Flop d_ff_13 (.D(d_ff_14_q), .clk(clock_4_out), .Q(d_ff_13_q), .preset(in_4), .reset(in_4));  // open: Qn
  Clock clock_5 (.out(clock_5_out));
  D_Flip_Flop d_ff_14 (.D(d_ff_16_q), .clk(clock_4_out), .Q(d_ff_14_q), .preset(in_4), .reset(in_4));  // open: Qn
  Multiplexer multiplexer_9 (.in0(D_FOR_R_SHIFT), .in1(d_ff_17_q), .out(multiplexer_9_out), .sel(SELECT));
  D_Flip_Flop d_ff_15 (
    .D(multiplexer_9_out), .clk(clock_5_out), .Q(d_ff_15_q), .preset(in_14), .reset(in_14));  // open: Qn
  LED led_13 (.in(d_ff_13_q));
  D_Flip_Flop d_ff_16 (.D(d_ff_18_q), .clk(clock_4_out), .Q(d_ff_16_q), .preset(in_4), .reset(in_4));  // open: Qn
  Multiplexer multiplexer_10 (.in0(d_ff_15_q), .in1(d_ff_19_q), .out(multiplexer_10_out), .sel(SELECT));
  D_Flip_Flop d_ff_17 (
    .D(multiplexer_10_out), .clk(clock_5_out), .Q(d_ff_17_q), .preset(in_14), .reset(in_14));  // open: Qn
  LED led_14 (.in(d_ff_14_q));
  LED led_15 (.in(d_ff_16_q));
  LED led_16 (.in(d_ff_18_q));
  D_Flip_Flop d_ff_18 (.D(in_2), .clk(clock_4_out), .Q(d_ff_18_q), .preset(in_4), .reset(in_4));  // open: Qn
  LED led_17 (.in(d_ff_15_q));
  LED led_18 (.in(d_ff_17_q));
  Multiplexer multiplexer_11 (.in0(d_ff_17_q), .in1(d_ff_20_q), .out(multiplexer_11_out), .sel(SELECT));
  D_Flip_Flop d_ff_19 (
    .D(multiplexer_11_out), .clk(clock_5_out), .Q(d_ff_19_q), .preset(in_14), .reset(in_14));  // open: Qn
  LED led_19 (.in(d_ff_19_q));
  LED led_20 (.in(d_ff_20_q));
  Multiplexer multiplexer_12 (.in0(d_ff_19_q), .in1(D_FOR_L_SHIFT), .out(multiplexer_12_out), .sel(SELECT));
  D_Flip_Flop d_ff_20 (
    .D(multiplexer_12_out), .clk(clock_5_out), .Q(d_ff_20_q), .preset(in_14), .reset(in_14));  // open: Qn

  // Notes on the sheet:
  //   00 ->LSHIFT
  //   01 ->RSHIFT
  //   11->RETAIN
  //   10->PARALLEL INPUT
  //   RIGHT
  //   R-SHIFT+ PARALLEL_INP
  //   UNIVERSAL SHIFT
  //   LEFT
  //   L_R_SHIFT
endmodule

module ctrs (
  input  selector,
  input  in_2,
  input  in_3,
  input  D,
  input  in_5,
  input  in_6,
  input  in_7,
  input  in_8,
  input  d_2,
  input  in_10,
  input  in_11,
  input  in_12,
  input  in_13,
  input  in_14,
  input  t,
  input  in_16,
  input  in_17,
  input  set,
  input  in_19,
  input  reset,
  input  in_21
);

  wire and_1_out, and_2_out, and_3_out, and_4_out, and_5_out, and_6_out, and_7_out, and_8_out, and_9_out,
       and_10_out, and_11_out, and_12_out, and_13_out, and_14_out, clock_1_out, clock_2_out, clock_3_out,
       clock_4_out, clock_5_out, clock_6_out, clock_7_out, d_ff_8_qn, not_1_out, t_ff_13_q, t_ff_13_qn,
       t_ff_14_q, t_ff_14_qn, t_ff_15_q, t_ff_15_qn, t_ff_16_q, t_ff_16_qn;
  wire [1:0] t_ff_18_q;
  wire [3:0] d_ff_4_q, d_ff_8_q, or_1_out, t_ff_7_q, t_ff_7_qn, t_ff_8_q, t_ff_8_qn, t_ff_12_q, t_ff_12_qn;

  LED led_1 (.in(t_ff_7_q[3]));
  and and_1 (and_1_out, and_2_out, t_ff_7_q[2]);
  T_Flip_Flop t_ff_1 (
    .T(and_1_out), .clk(clock_2_out), .Q(t_ff_7_q[3]), .Qn(t_ff_7_qn[3]), .reset(in_5), .preset(in_2));
  LED led_2 (.in(t_ff_8_q[3]));
  T_Flip_Flop #(.trigger("falling")) t_ff_2 (
    .T(t), .clk(t_ff_8_q[2]), .Q(t_ff_8_q[3]), .Qn(t_ff_8_qn[3]), .reset(in_16), .preset(in_17));
  T_Flip_Flop t_ff_3 (
    .T(and_2_out), .clk(clock_2_out), .Q(t_ff_7_q[2]), .Qn(t_ff_7_qn[2]), .reset(in_5), .preset(in_2));
  LED led_3 (.in(t_ff_8_q[2]));
  T_Flip_Flop #(.trigger("falling")) t_ff_4 (
    .T(t), .clk(t_ff_8_q[1]), .Q(t_ff_8_q[2]), .Qn(t_ff_8_qn[2]), .reset(in_16), .preset(in_17));
  LED led_4 (.in(t_ff_7_q[2]));
  and and_2 (and_2_out, t_ff_7_q[0], t_ff_7_q[1]);
  T_Flip_Flop t_ff_5 (
    .T(t_ff_7_q[0]), .clk(clock_2_out), .Q(t_ff_7_q[1]), .Qn(t_ff_7_qn[1]), .reset(in_5), .preset(in_2));
  LED led_5 (.in(t_ff_8_q[1]));
  T_Flip_Flop #(.trigger("falling")) t_ff_6 (
    .T(t), .clk(t_ff_8_q[0]), .Q(t_ff_8_q[1]), .Qn(t_ff_8_qn[1]), .reset(in_16), .preset(in_17));
  LED led_6 (.in(t_ff_7_q[1]));
  T_Flip_Flop t_ff_7 (.T(D), .clk(clock_2_out), .Q(t_ff_7_q[0]), .Qn(t_ff_7_qn[0]), .reset(in_5), .preset(in_2));
  LED led_7 (.in(t_ff_8_q[0]));
  T_Flip_Flop #(.trigger("falling")) t_ff_8 (
    .T(t), .clk(clock_1_out), .Q(t_ff_8_q[0]), .Qn(t_ff_8_qn[0]), .reset(in_16), .preset(in_17));
  Clock clock_1 (.out(clock_1_out));
  LED led_8 (.in(t_ff_7_q[0]));
  Clock clock_2 (.out(clock_2_out));
  Hex_Digit_Display #(.decimalPoint("false")) hex_digit_display_1 (.value(t_ff_8_q));
  Hex_Digit_Display #(.decimalPoint("false")) hex_digit_display_2 (.value(t_ff_8_qn));
  Hex_Digit_Display #(.decimalPoint("false")) hex_digit_display_3 (.value(t_ff_7_q));
  Hex_Digit_Display #(.decimalPoint("false")) hex_digit_display_4 (.value(t_ff_7_qn));
  T_Flip_Flop t_ff_9 (
    .T(and_3_out), .clk(clock_4_out), .Q(t_ff_12_q[3]), .Qn(t_ff_12_qn[3]), .reset(in_8), .preset(in_6));
  LED led_9 (.in(t_ff_12_q[3]));
  and and_3 (and_3_out, and_4_out, t_ff_12_qn[2]);
  Clock clock_3 (.out(clock_3_out));
  LED led_10 (.in(t_ff_12_q[2]));
  and and_4 (and_4_out, t_ff_12_qn[0], t_ff_12_qn[1]);
  T_Flip_Flop t_ff_10 (
    .T(and_4_out), .clk(clock_4_out), .Q(t_ff_12_q[2]), .Qn(t_ff_12_qn[2]), .reset(in_8), .preset(in_6));
  D_Flip_Flop d_ff_1 (.D(d_ff_4_q[3]), .clk(clock_3_out), .Q(d_ff_4_q[0]), .preset(set), .reset(reset));  // open: Qn
  LED led_11 (.in(t_ff_12_q[1]));
  T_Flip_Flop t_ff_11 (
    .T(t_ff_12_qn[0]), .clk(clock_4_out), .Q(t_ff_12_q[1]), .Qn(t_ff_12_qn[1]), .reset(in_8), .preset(in_6));
  D_Flip_Flop d_ff_2 (.D(d_ff_4_q[0]), .clk(clock_3_out), .Q(d_ff_4_q[1]), .reset(reset));  // open: Qn, preset
  LED led_12 (.in(t_ff_12_q[0]));
  T_Flip_Flop t_ff_12 (.T(in_7), .clk(clock_4_out), .Q(t_ff_12_q[0]), .Qn(t_ff_12_qn[0]), .reset(in_8), .preset(in_6));
  Hex_Digit_Display #(.decimalPoint("false")) hex_digit_display_5 (.value(d_ff_4_q));
  LED led_13 (.in(d_ff_4_q[0]));
  D_Flip_Flop d_ff_3 (.D(d_ff_4_q[1]), .clk(clock_3_out), .Q(d_ff_4_q[2]), .reset(reset));  // open: Qn, preset
  Clock clock_4 (.out(clock_4_out));
  LED led_14 (.in(d_ff_4_q[1]));
  LED led_15 (.in(d_ff_4_q[2]));
  Hex_Digit_Display #(.decimalPoint("false")) hex_digit_display_6 (.value(t_ff_12_q));
  Hex_Digit_Display #(.decimalPoint("false")) hex_digit_display_7 (.value(t_ff_12_qn));
  LED led_16 (.in(d_ff_4_q[3]));
  D_Flip_Flop d_ff_4 (.D(d_ff_4_q[2]), .clk(clock_3_out), .Q(d_ff_4_q[3]), .reset(reset));  // open: Qn, preset
  Hex_Digit_Display #(.decimalPoint("false")) hex_digit_display_8 (.value({d_ff_4_q[0], d_ff_4_q[1], d_ff_4_q[2], d_ff_4_q[3]}));
  T_Flip_Flop t_ff_13 (.T(and_5_out), .clk(clock_6_out), .Q(t_ff_13_q), .Qn(t_ff_13_qn), .reset(in_12), .preset(in_10));
  LED led_17 (.in(t_ff_13_qn));
  LED led_18 (.in(t_ff_13_q));
  and and_5 (and_5_out, and_6_out, t_ff_14_q);
  D_Flip_Flop d_ff_5 (.D(d_ff_8_qn), .clk(clock_5_out), .Q(d_ff_8_q[0]), .preset(in_19), .reset(in_21));  // open: Qn
  Clock clock_5 (.out(clock_5_out));
  LED led_19 (.in(t_ff_14_q));
  and and_6 (and_6_out, t_ff_16_q, t_ff_15_q);
  T_Flip_Flop t_ff_14 (.T(and_6_out), .clk(clock_6_out), .Q(t_ff_14_q), .Qn(t_ff_14_qn), .reset(in_12), .preset(in_10));
  LED led_20 (.in(t_ff_14_qn));
  LED led_21 (.in(t_ff_15_q));
  T_Flip_Flop t_ff_15 (.T(t_ff_16_q), .clk(clock_6_out), .Q(t_ff_15_q), .Qn(t_ff_15_qn), .reset(in_12), .preset(in_10));
  Hex_Digit_Display #(.decimalPoint("false")) hex_digit_display_9 (.value(d_ff_8_q));
  D_Flip_Flop d_ff_6 (.D(d_ff_8_q[0]), .clk(clock_5_out), .Q(d_ff_8_q[1]), .reset(in_21));  // open: Qn, preset
  LED led_22 (.in(t_ff_16_q));
  T_Flip_Flop t_ff_16 (.T(in_11), .clk(clock_6_out), .Q(t_ff_16_q), .Qn(t_ff_16_qn), .reset(in_12), .preset(in_10));
  LED led_23 (.in(t_ff_15_qn));
  LED led_24 (.in(d_ff_8_q[0]));
  LED led_25 (.in(d_ff_8_q[1]));
  D_Flip_Flop d_ff_7 (.D(d_ff_8_q[1]), .clk(clock_5_out), .Q(d_ff_8_q[2]), .reset(in_21));  // open: Qn, preset
  Clock clock_6 (.out(clock_6_out));
  LED led_26 (.in(t_ff_16_qn));
  LED led_27 (.in(d_ff_8_q[2]));
  LED led_28 (.in(d_ff_8_q[3]));
  D_Flip_Flop d_ff_8 (
    .D(d_ff_8_q[2]), .clk(clock_5_out), .Q(d_ff_8_q[3]), .Qn(d_ff_8_qn), .reset(in_21));  // open: preset
  Hex_Digit_Display #(.decimalPoint("false")) hex_digit_display_10 (.value({d_ff_8_q[0], d_ff_8_q[1], d_ff_8_q[2], d_ff_8_q[3]}));
  not not_1 (not_1_out, selector);
  and and_7 (and_7_out, not_1_out, t_ff_16_q);
  and and_8 (and_8_out, t_ff_16_qn, selector);
  and and_9 (and_9_out, not_1_out, t_ff_15_q);
  and and_10 (and_10_out, t_ff_15_qn, selector);
  and and_11 (and_11_out, not_1_out, t_ff_14_q);
  and and_12 (and_12_out, t_ff_14_qn, selector);
  and and_13 (and_13_out, not_1_out, t_ff_13_q);
  and and_14 (and_14_out, t_ff_13_qn, selector);
  or or_1 (or_1_out[0], and_7_out, and_8_out);
  or or_2 (or_1_out[1], and_9_out, and_10_out);
  or or_3 (or_1_out[2], and_11_out, and_12_out);
  or or_4 (or_1_out[3], and_13_out, and_14_out);
  Hex_Digit_Display #(.decimalPoint("false")) hex_digit_display_11 (.value(or_1_out));
  T_Flip_Flop t_ff_17 (
    .T(t_ff_18_q[0]), .clk(clock_7_out), .Q(t_ff_18_q[1]), .reset(in_13), .preset(in_14));  // open: Qn
  LED led_29 (.in(t_ff_18_q[1]));
  T_Flip_Flop t_ff_18 (.T(d_2), .clk(clock_7_out), .Q(t_ff_18_q[0]), .reset(in_13), .preset(in_14));  // open: Qn
  LED led_30 (.in(t_ff_18_q[0]));
  Hex_Digit_Display #(.decimalPoint("false")) hex_digit_display_12 (.value({{2{in_3}}, t_ff_18_q}));
  Clock clock_7 (.out(clock_7_out));

  // Notes on the sheet:
  //   ASYNC-COUNTER
  //   SYNC -UP-DOWN/ COUNTER(M-1)
  //   (FALLING EDGE)
  //   RISING EDGE
  //   O->UP COUNTER
  //   O'->DOWN COUNTER
  //   DOWN COUNTER
  //   O->UP COUNTER
  //   O'->DOWN COUNTER
  //   UP COUNTER
  //   UP-COUNTER
  //   DOWN COUNTER
  //   SYNC -UP-DOWN/ COUNTER(M-2)
  //   1-->2-->4--->8
  //   RING-COUNTER (D FF)
  //   RISING EDGE
  //   8-->4-->2-->1
  //   O->UP COUNTER
  //   O'->DOWN COUNTER
  //   DOWN COUNTER
  //   UP-COUNTER
  //   SINGLE SYNC -UP-DOWN/ COUNTER(M-3)
  //   1-->3-->7-->15
  //   RISING EDGE
  //   JOHNSON-COUNTER (D FF)
  //   15-->7-->3-->1
  //   O->UP COUNTER
  //   O'->DOWN COUNTER
  //   0 - UP-COUNTER
  //   1- DOWN COUNTER
  //   6 BIT UP COUNTER(VIA 2 BIT SYNC UP + 7493 ASYNC 4 BIT UP)
  //   RISING EDGE
  //   UP-COUNTER
endmodule
