// Logisim project UNIVERSAL_SHIFT_REGISTER.circ as structural Verilog: 1 circuit, main circuit main
module main (
  input  in_1,
  input  in_2,
  input  in_3,
  input  in_4,
  input  DATARIGHT,
  input  DATALEFT,
  input  [1:0] SELECTOR,
  input  SET,
  input  RESET
);

  wire clock_1_out, d_ff_1_q, d_ff_2_q, d_ff_3_q, d_ff_4_q, multiplexer_1_out, multiplexer_2_out,
       multiplexer_3_out, multiplexer_4_out;

  Clock clock_1 (.out(clock_1_out));
  LED led_1 (.in(d_ff_1_q));
  Multiplexer #(.select(2)) multiplexer_1 (
    .in0(DATALEFT), .in1(d_ff_2_q), .in2(in_1), .in3(d_ff_1_q), .out(multiplexer_1_out), .sel(SELECTOR));
  D_Flip_Flop d_ff_1 (.D(multiplexer_1_out), .clk(clock_1_out), .Q(d_ff_1_q), .preset(SET), .reset(RESET));  // open: Qn
  LED led_2 (.in(d_ff_2_q));
  Multiplexer #(.select(2)) multiplexer_2 (
    .in0(d_ff_1_q), .in1(d_ff_3_q), .in2(in_2), .in3(d_ff_2_q), .out(multiplexer_2_out), .sel(SELECTOR));
  D_Flip_Flop d_ff_2 (.D(multiplexer_2_out), .clk(clock_1_out), .Q(d_ff_2_q), .preset(SET), .reset(RESET));  // open: Qn
  LED led_3 (.in(d_ff_3_q));
  LED led_4 (.in(d_ff_4_q));
  Multiplexer #(.select(2)) multiplexer_3 (
    .in0(d_ff_2_q), .in1(d_ff_4_q), .in2(in_3), .in3(d_ff_3_q), .out(multiplexer_3_out), .sel(SELECTOR));
  D_Flip_Flop d_ff_3 (.D(multiplexer_3_out), .clk(clock_1_out), .Q(d_ff_3_q), .preset(SET), .reset(RESET));  // open: Qn
  D_Flip_Flop d_ff_4 (.D(multiplexer_4_out), .clk(clock_1_out), .Q(d_ff_4_q), .preset(SET), .reset(RESET));  // open: Qn
  Multiplexer #(.select(2)) multiplexer_4 (
    .in0(d_ff_3_q), .in1(DATARIGHT), .in2(in_4), .in3(d_ff_4_q), .out(multiplexer_4_out), .sel(SELECTOR));

  // Notes on the sheet:
  //   00 ->LSHIFT
  //   01 ->RSHIFT
  //   11->RETAIN
  //   10->PARALLEL INPUT
endmodule
